// Logisim project Real_Alu.circ as structural Verilog: 8 circuits, main circuit In_A AND In_B
module In_A_AND_In_B (
  input  [7:0] In_A,
  input  [7:0] In_B,
  output [7:0] Alu_out
);

  assign Alu_out = In_A & In_B;  // AND_Gate and_1, 8 bits wide
endmodule

module In_a_OR_In_B (
  input  [7:0] In_A,
  input  [7:0] In_B,
  output [7:0] Alu_Out
);

  assign Alu_Out = In_A | In_B;  // OR_Gate or_1, 8 bits wide
endmodule

module Not_In_B (
  input  [7:0] In_B,
  output [7:0] Alu_Out
);

  assign Alu_Out = ~In_B;  // NOT_Gate not_1, 8 bits wide
endmodule

module Shift_to_left (
  input  D0,
  input  D1,
  input  D2,
  input  D3,
  input  D4,
  input  D5,
  input  D6,
  input  D7,
  output S0,
  output S1,
  output S2,
  output S3,
  output S4,
  output S5,
  output S7,
  output S6
);

  wire and_1_out, and_4_out, and_6_out, and_8_out, and_10_out, and_14_out, x2, x3, x4, x5, x6, x7;

  and and_1 (and_1_out, D0, 1'b0);
  and and_2 (S0, 1'b1, D1);
  or or_1 (S1, and_1_out, x2);
  and and_3 (x5, 1'b1, D5);
  and and_4 (and_4_out, D5, 1'b0);
  or or_2 (S6, and_4_out, x7);
  and and_5 (x2, 1'b1, D2);
  and and_6 (and_6_out, D1, 1'b0);
  or or_3 (S2, and_6_out, x3);
  and and_7 (x6, 1'b1, D6);
  and and_8 (and_8_out, D2, 1'b0);
  or or_4 (S3, and_8_out, x4);
  and and_9 (S7, D6, 1'b0);
  and and_10 (and_10_out, D3, 1'b0);
  and and_11 (x3, 1'b1, D3);
  or or_5 (S4, and_10_out, x5);
  and and_12 (x7, D7, 1'b1);
  and and_13 (x4, 1'b1, D4);
  and and_14 (and_14_out, D4, 1'b0);
  or or_6 (S5, and_14_out, x6);

  // Other names for the same wires on the sheet: _0 = D0; _1 = D1; _2 = D2; _3 = D3; _4 = D4; _5 = D5; _6 = D6;
  //   _7 = D7
endmodule

module Shift_to_right (
  input  D0,
  input  D1,
  input  D2,
  input  D3,
  input  D4,
  input  D5,
  input  D6,
  input  D7,
  output S0,
  output S1,
  output S2,
  output S3,
  output S4,
  output S5,
  output S7,
  output S6
);

  wire and_1_out, and_4_out, and_6_out, and_8_out, and_10_out, and_13_out, x2, x3, x4, x5, x6, x7;

  and and_1 (and_1_out, D0, 1'b1);
  and and_2 (S0, 1'b0, D1);
  or or_1 (S1, and_1_out, x2);
  and and_3 (x5, 1'b0, D5);
  and and_4 (and_4_out, D5, 1'b1);
  or or_2 (S6, and_4_out, x7);
  and and_5 (x2, 1'b0, D2);
  and and_6 (and_6_out, D1, 1'b1);
  or or_3 (S2, and_6_out, x3);
  and and_7 (x6, 1'b0, D6);
  and and_8 (and_8_out, D2, 1'b1);
  or or_4 (S3, and_8_out, x4);
  and and_9 (S7, D6, 1'b1);
  and and_10 (and_10_out, D3, 1'b1);
  and and_11 (x3, 1'b0, D3);
  or or_5 (S4, and_10_out, x5);
  and and_12 (x7, D7, 1'b0);
  and and_13 (and_13_out, D4, 1'b1);
  and and_14 (x4, 1'b0, D4);
  or or_6 (S5, and_13_out, x6);

  // Other names for the same wires on the sheet: _0 = D0; _1 = D1; _2 = D2; _3 = D3; _4 = D4; _5 = D5; _6 = D6;
  //   _7 = D7
endmodule

module in_A_ADD_in_B (
  input  [7:0] A,
  input  [7:0] B,
  output C
);

  wire _0, _1, _2, _3, _4, _5, _6, _7, C1, full_adder_1_c1, full_adder_2_c1, full_adder_3_c1,
       full_adder_4_c1, full_adder_5_c1, half_adder_1_c;

  half_adder half_adder_1 (.S(_0), .C(half_adder_1_c), .A(A[0]), .B(B[0]));
  full_adder full_adder_1 (.S(_4), .C1(full_adder_1_c1), .C0(C1), .A(A[4]), .B(B[4]));
  full_adder full_adder_2 (.S(_1), .C1(full_adder_2_c1), .C0(half_adder_1_c), .A(A[1]), .B(B[1]));
  full_adder full_adder_3 (.S(_5), .C1(full_adder_3_c1), .C0(full_adder_1_c1), .A(A[5]), .B(B[5]));
  full_adder full_adder_4 (.S(_2), .C1(full_adder_4_c1), .C0(full_adder_2_c1), .A(A[2]), .B(B[2]));
  full_adder full_adder_5 (.S(_6), .C1(full_adder_5_c1), .C0(full_adder_3_c1), .A(A[6]), .B(B[6]));
  full_adder full_adder_6 (.S(_3), .C1(C1), .C0(full_adder_4_c1), .A(A[3]), .B(B[3]));
  full_adder full_adder_7 (.S(_7), .C1(C), .C0(full_adder_5_c1), .A(A[7]), .B(B[7]));
endmodule

module half_adder (
  input  A,
  input  B,
  output S,
  output C
);

  xor xor_1 (S, B, A);
  and and_1 (C, B, A);
endmodule

module full_adder (
  input  C0,
  input  A,
  input  B,
  output S,
  output C1
);

  wire and_1_out, and_2_out, and_3_out, xor_1_out;

  xor xor_1 (xor_1_out, B, A);
  xor xor_2 (S, xor_1_out, C0);
  and and_1 (and_1_out, A, C0);
  and and_2 (and_2_out, B, A);
  and and_3 (and_3_out, B, C0);
  or or_1 (C1, and_1_out, and_2_out, and_3_out);
endmodule
